// Logisim project processor.circ as structural Verilog: 5 circuits, main circuit main
module main (
  input  [31:0] Instruction,
  input  [1:0] in_2,
  input  [31:0] data1,
  input  [3:0] SELECTOR,
  input  [31:0] data2,
  input  [4:0] in_6,
  input  in_7,
  input  in_8,
  output [31:0] out_9,
  output [31:0] out_10
);

  wire clock_1_out, not_1_out, not_2_out, undriven;
  wire [3:0] decode_1_out_2;
  wire [4:0] FUNCT3, RD, RS1, RS2;
  wire [5:0] FUNCT7, OPCODE, register_7_q;
  wire [31:0] alu_1_out_4, register_1_q, register_8_q, register_9_q;

  Register #(.width(32)) register_1 (.D(Instruction), .Q(register_1_q), .clk(clock_1_out));  // open: en, clr
  IF if_1 (
    .Instruction(register_1_q), .in_2(in_2), .OPCODE(OPCODE), .RD(RD), .FUNCT3(FUNCT3), .RS1(RS1), .RS2(RS2),
    .FUNCT7(FUNCT7));
  Clock clock_1 (.out(clock_1_out));
  Register #(.width(6)) register_2 (.D(OPCODE), .clk(clock_1_out));  // open: en, Q, clr
  Register #(.width(5)) register_3 (.D(RD), .clk(clock_1_out));  // open: en, Q, clr
  Register #(.width(5)) register_4 (.D(FUNCT3), .clk(clock_1_out));  // open: en, Q, clr
  Register #(.width(5)) register_5 (.D(RS1), .clk(clock_1_out));  // open: en, Q, clr
  Register #(.width(5)) register_6 (.D(RS2), .clk(clock_1_out));  // open: en, Q, clr
  Register #(.width(6)) register_7 (.D(FUNCT7), .Q(register_7_q), .clk(clock_1_out));  // open: en, clr
  Register #(.width(32)) register_8 (.D(data1), .Q(register_8_q), .clk(clock_1_out));  // open: en, clr
  Register #(.width(32)) register_9 (.D(data2), .Q(register_9_q), .clk(clock_1_out));  // open: en, clr
  Decode decode_1 (.in_1(register_7_q), .out_2(decode_1_out_2));
  ALU alu_1 (.RS1(register_8_q), .RS2(register_9_q), .SELECTOR(decode_1_out_2), .out_4(alu_1_out_4));
  Register #(.width(32)) register_10 (.D(alu_1_out_4), .Q(out_9), .clk(clock_1_out));  // open: en, clr
  not not_1 (not_1_out, in_7);
  not not_2 (not_2_out, in_8);
  RAM #(.addrWidth(5), .dataWidth(32), .bus("separate")) ram_1 (
    .addr(in_6), .data(out_10), .str(not_2_out), .sel(not_1_out), .clk(undriven), .ld(in_8));  // open: din, clr

  // Other names for the same wires on the sheet: R_I_J_TYPE[1:0] = in_2
endmodule

// Arithmetic Logic Unit
module ALU (
  input  [31:0] RS1,
  input  [31:0] RS2,
  input  [3:0] SELECTOR,
  output [31:0] out_4
);

  wire comparator_1_eq, comparator_1_gt, comparator_1_lt;
  wire [31:0] adder_1_out, and_1_out, bit_extender_1_out, bit_extender_2_out, bit_extender_3_out,
       divider_1_out, multiplier_1_out, not_1_out, or_1_out, subtractor_1_out;

  Adder #(.width(32)) adder_1 (.a(RS1), .b(RS2), .out(adder_1_out));  // open: cin, cout
  Subtractor #(.width(32)) subtractor_1 (.a(RS1), .b(RS2), .out(subtractor_1_out));  // open: bin, bout
  Multiplier #(.width(32)) multiplier_1 (.a(RS1), .b(RS2), .out(multiplier_1_out));  // open: cin, cout
  Divider #(.width(32)) divider_1 (.a(RS1), .b(RS2), .out(divider_1_out));  // open: upper, rem
  assign and_1_out = RS1 & RS2;  // AND_Gate and_1, 32 bits wide
  assign not_1_out = ~RS1;  // NOT_Gate not_1, 32 bits wide
  assign or_1_out = RS1 | RS2;  // OR_Gate or_1, 32 bits wide
  Comparator #(.width(32)) comparator_1 (
    .a(RS1), .b(RS2), .gt(comparator_1_gt), .eq(comparator_1_eq), .lt(comparator_1_lt));
  assign bit_extender_1_out = {{31{1'b0}}, comparator_1_gt};  // Bit_Extender bit_extender_1
  assign bit_extender_2_out = {{31{1'b0}}, comparator_1_eq};  // Bit_Extender bit_extender_2
  assign bit_extender_3_out = {{31{1'b0}}, comparator_1_lt};  // Bit_Extender bit_extender_3
  Multiplexer #(.select(4), .width(32)) multiplexer_1 (
    .in0(adder_1_out), .in1(subtractor_1_out), .in2(multiplier_1_out), .in3(divider_1_out), .in4(and_1_out),
    .in5(not_1_out), .in6(or_1_out), .in7(bit_extender_1_out), .in8(bit_extender_2_out),
    .in9(bit_extender_3_out), .out(out_4), .sel(SELECTOR));  // open: in10, in11, in12, in13, in14, in15, en
endmodule

module Decode (
  input  [5:0] in_1,
  output [3:0] out_2
);

  Bit_Extender #(.in_width(6), .out_width(4)) bit_extender_1 (.in(in_1), .out(out_2));

  // Other names for the same wires on the sheet: Funct7_ID[5:0] = in_1
endmodule

module IF (
  input  [31:0] Instruction,
  input  [1:0] in_2,
  output [5:0] OPCODE,
  output [4:0] RD,
  output [4:0] FUNCT3,
  output [4:0] RS1,
  output [4:0] RS2,
  output [5:0] FUNCT7
);

  Multiplexer #(.select(2), .width(6)) multiplexer_1 (
    .in0(Instruction[5:0]), .out(OPCODE), .sel(in_2));  // open: in1, in2, in3, en
  Multiplexer #(.select(2), .width(5)) multiplexer_2 (
    .in0(Instruction[10:6]), .out(RD), .sel(in_2));  // open: in1, in2, in3, en
  Multiplexer #(.select(2), .width(5)) multiplexer_3 (
    .in0(Instruction[15:11]), .out(FUNCT3), .sel(in_2));  // open: in1, in2, in3, en
  Multiplexer #(.select(2), .width(5)) multiplexer_4 (
    .in0(Instruction[20:16]), .out(RS1), .sel(in_2));  // open: in1, in2, in3, en
  Multiplexer #(.select(2), .width(5)) multiplexer_5 (
    .in0(Instruction[25:21]), .out(RS2), .sel(in_2));  // open: in1, in2, in3, en
  Multiplexer #(.select(2), .width(6)) multiplexer_6 (
    .in0(Instruction[31:26]), .out(FUNCT7), .sel(in_2));  // open: in1, in2, in3, en
  // Probe on nothing
endmodule

module Register_File (
  input  [4:0] in_1,
  input  [4:0] in_2
);

  Register RS1 ();  // open: D, en, Q, clk, clr
  Multiplexer #(.select(5)) multiplexer_1 (.sel(in_1));  // open: in0, in1, in2, in3, in4, in5, in6, in7, in8, in9, in10, in11, in12, in13, in14, in15, in16, in17, in18, in19, in20, in21, in22, in23, in24, in25, in26, in27, in28, in29, in30, in31, out, en
  Multiplexer #(.select(5)) multiplexer_2 (.sel(in_2));  // open: in0, in1, in2, in3, in4, in5, in6, in7, in8, in9, in10, in11, in12, in13, in14, in15, in16, in17, in18, in19, in20, in21, in22, in23, in24, in25, in26, in27, in28, in29, in30, in31, out, en
endmodule
